# Fritzing sketch pcb-in-a-box (saved by Fritzing 0.7.12b)
breadboards: 1
perfboards: 10

parts:
  Arduino1 = Arduino
  LCD1 = LCD screen
  LED1 = Blue LED - 5mm
  LED2 = Blue LED - 5mm
  LED3 = Blue LED - 5mm
  LED4 = Blue LED - 5mm
  LED5 = Blue LED - 5mm
  LED6 = Blue LED - 5mm
  R7 = 10 Ω Resistor [package=THT]
  R8 = 10 Ω Resistor [package=THT]
  LED7 = green LED - 5mm
  LED8 = LED - 5mm [color="Red (633nm)" package="5 mm [THT]"]
  S1 = Pushbutton [package="[THT]"]
  S2 = Pushbutton [package="[THT]"]
  Power_plug1 = Power plug
  Q3 = NPN-Transistor [package="TO92 [THT]"]
  R4 = Trimmer Potentiometer [maximum_resistance=10kΩ package=THT]
  R2 = Dial Potentiometer with switch [maximum_resistance=100kΩ]
  Q4 = NPN-Transistor [package="TO92 [THT]"]
  R9 = 1k Ω Resistor [package=THT]
  R10 = 1k Ω Resistor [package=THT]
  R11 = 680 Ω Resistor [package=THT]
  R15 = 680 Ω Resistor [package=THT]
  R16 = 680 Ω Resistor [package=THT]
  R12 = 680 Ω Resistor [package=THT]
  R13 = 680 Ω Resistor [package=THT]
  R14 = 680 Ω Resistor [package=THT]
  LED9 = Blue LED - 5mm
  LED10 = Blue LED - 5mm
  LED11 = Blue LED - 5mm
  LED12 = Blue LED - 5mm
  LED13 = Blue LED - 5mm
  LED14 = Blue LED - 5mm
  LED15 = Blue LED - 5mm
  LED16 = Blue LED - 5mm
  LED17 = Blue LED - 5mm
  LED18 = Blue LED - 5mm
  R17 = 680 Ω Resistor [package=THT]
  R18 = 680 Ω Resistor [package=THT]
  R19 = 680 Ω Resistor [package=THT]
  R20 = 680 Ω Resistor [package=THT]
  R21 = 680 Ω Resistor [package=THT]
  R22 = 680 Ω Resistor [package=THT]
  R23 = 680 Ω Resistor [package=THT]
  R24 = 680 Ω Resistor [package=THT]
  R25 = 680 Ω Resistor [package=THT]
  R26 = 680 Ω Resistor [package=THT]
  Q5 = NPN-Transistor [package="TO92 [THT]"]
  R27 = 1k Ω Resistor [package=THT]
  R28 = 1k Ω Resistor [package=THT]
  Q6 = NPN-Transistor [package="TO92 [THT]"]
  R29 = 1k Ω Resistor [package=THT]
  Q7 = NPN-Transistor [package="TO92 [THT]"]
  R30 = 1k Ω Resistor [package=THT]
  Q8 = NPN-Transistor [package="TO92 [THT]"]
  LED19 = Blue LED - 5mm
  LED20 = Blue LED - 5mm
  LED21 = Blue LED - 5mm
  LED22 = Blue LED - 5mm
  LED23 = Blue LED - 5mm
  LED24 = Blue LED - 5mm
  LED25 = Blue LED - 5mm
  LED26 = Blue LED - 5mm
  R31 = 680 Ω Resistor [package=THT]
  R32 = 680 Ω Resistor [package=THT]
  R33 = 680 Ω Resistor [package=THT]
  R34 = 680 Ω Resistor [package=THT]
  R35 = 680 Ω Resistor [package=THT]
  R36 = 680 Ω Resistor [package=THT]
  R37 = 680 Ω Resistor [package=THT]
  R38 = 680 Ω Resistor [package=THT]
  R39 = 680 Ω Resistor [package=THT]
  R40 = 680 Ω Resistor [package=THT]
  R41 = 680 Ω Resistor [package=THT]
  R42 = 680 Ω Resistor [package=THT]
  R43 = 680 Ω Resistor [package=THT]
  R44 = 680 Ω Resistor [package=THT]
  R45 = 680 Ω Resistor [package=THT]
  R46 = 680 Ω Resistor [package=THT]
  LED27 = Blue LED - 5mm
  LED28 = Blue LED - 5mm
  LED29 = Blue LED - 5mm
  LED30 = Blue LED - 5mm
  LED31 = Blue LED - 5mm
  LED32 = Blue LED - 5mm
  LED33 = Blue LED - 5mm
  LED34 = Blue LED - 5mm
  LED35 = Blue LED - 5mm
  LED36 = Blue LED - 5mm
  LED37 = Blue LED - 5mm
  LED38 = Blue LED - 5mm
  LED39 = Blue LED - 5mm
  LED40 = Blue LED - 5mm
  LED41 = Blue LED - 5mm
  LED42 = Blue LED - 5mm
  R47 = 680 Ω Resistor [package=THT]
  R48 = 680 Ω Resistor [package=THT]
  R49 = 680 Ω Resistor [package=THT]
  R50 = 680 Ω Resistor [package=THT]
  R51 = 680 Ω Resistor [package=THT]
  R52 = 680 Ω Resistor [package=THT]
  R53 = 680 Ω Resistor [package=THT]
  R54 = 680 Ω Resistor [package=THT]
  R55 = 680 Ω Resistor [package=THT]
  R56 = 680 Ω Resistor [package=THT]
  R57 = 680 Ω Resistor [package=THT]
  R58 = 680 Ω Resistor [package=THT]
  R59 = 680 Ω Resistor [package=THT]
  R60 = 680 Ω Resistor [package=THT]
  R61 = 680 Ω Resistor [package=THT]
  R62 = 680 Ω Resistor [package=THT]
  LED43 = Blue LED - 5mm
  LED44 = Blue LED - 5mm
  LED45 = Blue LED - 5mm
  LED46 = Blue LED - 5mm
  LED47 = Blue LED - 5mm
  LED48 = Blue LED - 5mm
  LED49 = Blue LED - 5mm
  LED50 = Blue LED - 5mm
  R1 = Dial Potentiometer with switch [maximum_resistance=100kΩ]
  LED51 = Blue LED - 5mm
  LED52 = Blue LED - 5mm
  LED53 = Blue LED - 5mm
  LED54 = Blue LED - 5mm
  LED55 = Blue LED - 5mm
  LED56 = Blue LED - 5mm
  LED57 = Blue LED - 5mm
  LED58 = Blue LED - 5mm
  R63 = 680 Ω Resistor [package=THT]
  R64 = 680 Ω Resistor [package=THT]
  R65 = 680 Ω Resistor [package=THT]
  R66 = 680 Ω Resistor [package=THT]
  R67 = 680 Ω Resistor [package=THT]
  R68 = 680 Ω Resistor [package=THT]
  R69 = 680 Ω Resistor [package=THT]
  R70 = 680 Ω Resistor [package=THT]
  R71 = 680 Ω Resistor [package=THT]
  R72 = 680 Ω Resistor [package=THT]
  R73 = 680 Ω Resistor [package=THT]
  R74 = 680 Ω Resistor [package=THT]
  R75 = 680 Ω Resistor [package=THT]
  R76 = 680 Ω Resistor [package=THT]
  R77 = 680 Ω Resistor [package=THT]
  R78 = 680 Ω Resistor [package=THT]
  LED59 = Blue LED - 5mm
  LED60 = Blue LED - 5mm
  LED61 = Blue LED - 5mm
  LED62 = Blue LED - 5mm
  LED63 = Blue LED - 5mm
  LED64 = Blue LED - 5mm
  LED65 = Blue LED - 5mm
  LED66 = Blue LED - 5mm
  R79 = 1k Ω Resistor [package=THT]
  R80 = 1k Ω Resistor [package=THT]
  Q9 = NPN-Transistor [package="TO92 [THT]"]
  Q10 = NPN-Transistor [package="TO92 [THT]"]

nets:
  GND: Arduino1.GND, LCD1.VSS, LCD1.R/W, LCD1.LED-, LED7.cathode, LED8.cathode, S1.Pin_1, S1.Pin_2, S2.Pin_1, S2.Pin_2, Power_plug1.GND, Q3.E, R4.leg2, R2.leg2, Q4.E, Q5.E, Q6.E, Q7.E, Q8.E, R1.leg2
  N1: Arduino1.D13, S1.Pin_3, S1.Pin_4
  N2: Arduino1.D12, R8.Pin_0
  N3: Arduino1.D11, R7.Pin_0
  N4: Arduino1.D10, R28.Pin_0, R29.Pin_0, R30.Pin_0, R79.Pin_0
  N5: Arduino1.D9, R9.Pin_0, R10.Pin_0, R27.Pin_0, R80.Pin_0
  N6: Arduino1.D8, S2.Pin_3, S2.Pin_4
  N7: Arduino1.D7, LCD1.RS
  N8: Arduino1.D6, LCD1.E
  N9: Arduino1.D5, LCD1.DB4
  N10: Arduino1.D4, LCD1.DB5
  N11: Arduino1.D3, LCD1.DB6
  N12: Arduino1.D2, LCD1.DB7
  5V: Arduino1.+5V, LCD1.VDD, LCD1.LED+, R4.leg1, R2.leg1, R1.leg1
  N13: Arduino1.A0, R1.wiper
  N14: Arduino1.A1, R2.wiper
  N15: LCD1.V0, R4.wiper
  N16: LED1.cathode, LED2.cathode, LED3.cathode, LED9.cathode, LED10.cathode, LED11.cathode, LED13.cathode, LED14.cathode, Q8.C
  N17: LED1.anode, R12.Pin_0
  N18: LED2.anode, R13.Pin_0
  N19: LED3.anode, R14.Pin_0
  N20: LED4.cathode, LED5.cathode, LED6.cathode, Q3.C, LED12.cathode, LED15.cathode, LED16.cathode, LED17.cathode, LED18.cathode
  N21: LED4.anode, R11.Pin_0
  N22: LED5.anode, R16.Pin_0
  N23: LED6.anode, R15.Pin_0
  N24: R7.Pin_1, LED8.anode
  N25: R8.Pin_1, LED7.anode
  N26: Power_plug1.VCC, R11.Pin_1, R15.Pin_1, R16.Pin_1, R12.Pin_1, R13.Pin_1, R14.Pin_1, R17.Pin_1, R18.Pin_1, R19.Pin_1, R20.Pin_1, R21.Pin_1, R22.Pin_1, R23.Pin_1, R24.Pin_1, R25.Pin_1, R26.Pin_1, R31.Pin_1, R32.Pin_1, R33.Pin_1, R34.Pin_1, R35.Pin_1, R36.Pin_1, R37.Pin_1, R38.Pin_1, R39.Pin_1, R40.Pin_1, R41.Pin_1, R42.Pin_1, R43.Pin_1, R44.Pin_1, R45.Pin_1, R46.Pin_1, R47.Pin_1, R48.Pin_1, R49.Pin_1, R50.Pin_1, R51.Pin_1, R52.Pin_1, R53.Pin_1, R54.Pin_1, R55.Pin_1, R56.Pin_1, R57.Pin_1, R58.Pin_1, R59.Pin_1, R60.Pin_1, R61.Pin_1, R62.Pin_1, R63.Pin_1, R64.Pin_1, R65.Pin_1, R66.Pin_1, R67.Pin_1, R68.Pin_1, R69.Pin_1, R70.Pin_1, R71.Pin_1, R72.Pin_1, R73.Pin_1, R74.Pin_1, R75.Pin_1, R76.Pin_1, R77.Pin_1, R78.Pin_1
  N27: Q3.B, R9.Pin_1
  N28: Q4.B, R10.Pin_1
  N29: Q4.C, LED35.cathode, LED36.cathode, LED37.cathode, LED38.cathode, LED39.cathode, LED40.cathode, LED41.cathode, LED42.cathode
  N30: LED9.anode, R23.Pin_0
  N31: LED10.anode, R18.Pin_0
  N32: LED11.anode, R24.Pin_0
  N33: LED12.anode, R22.Pin_0
  N34: LED13.anode, R25.Pin_0
  N35: LED14.anode, R17.Pin_0
  N36: LED15.anode, R20.Pin_0
  N37: LED16.anode, R19.Pin_0
  N38: LED17.anode, R21.Pin_0
  N39: LED18.anode, R26.Pin_0
  N40: Q5.B, R27.Pin_1
  N41: Q5.C, LED19.cathode, LED20.cathode, LED21.cathode, LED22.cathode, LED23.cathode, LED24.cathode, LED25.cathode, LED26.cathode
  N42: R28.Pin_1, Q6.B
  N43: Q6.C, LED43.cathode, LED44.cathode, LED45.cathode, LED46.cathode, LED47.cathode, LED48.cathode, LED49.cathode, LED50.cathode
  N44: R29.Pin_1, Q7.B
  N45: Q7.C, LED27.cathode, LED28.cathode, LED29.cathode, LED30.cathode, LED31.cathode, LED32.cathode, LED33.cathode, LED34.cathode
  N46: R30.Pin_1, Q8.B
  N47: LED19.anode, R33.Pin_0
  N48: LED20.anode, R32.Pin_0
  N49: LED21.anode, R31.Pin_0
  N50: LED22.anode, R38.Pin_0
  N51: LED23.anode, R35.Pin_0
  N52: LED24.anode, R34.Pin_0
  N53: LED25.anode, R36.Pin_0
  N54: LED26.anode, R37.Pin_0
  N55: R39.Pin_0, LED32.anode
  N56: R40.Pin_0, LED28.anode
  N57: R41.Pin_0, LED31.anode
  N58: R42.Pin_0, LED27.anode
  N59: R43.Pin_0, LED30.anode
  N60: R44.Pin_0, LED33.anode
  N61: R45.Pin_0, LED34.anode
  N62: R46.Pin_0, LED29.anode
  N63: LED35.anode, R49.Pin_0
  N64: LED36.anode, R48.Pin_0
  N65: LED37.anode, R47.Pin_0
  N66: LED38.anode, R54.Pin_0
  N67: LED39.anode, R51.Pin_0
  N68: LED40.anode, R50.Pin_0
  N69: LED41.anode, R52.Pin_0
  N70: LED42.anode, R53.Pin_0
  N71: R55.Pin_0, LED48.anode
  N72: R56.Pin_0, LED44.anode
  N73: R57.Pin_0, LED47.anode
  N74: R58.Pin_0, LED43.anode
  N75: R59.Pin_0, LED46.anode
  N76: R60.Pin_0, LED49.anode
  N77: R61.Pin_0, LED50.anode
  N78: R62.Pin_0, LED45.anode
  N79: LED51.cathode, LED52.cathode, LED53.cathode, LED54.cathode, LED55.cathode, LED56.cathode, LED57.cathode, LED58.cathode, Q9.C
  N80: LED51.anode, R65.Pin_0
  N81: LED52.anode, R64.Pin_0
  N82: LED53.anode, R63.Pin_0
  N83: LED54.anode, R70.Pin_0
  N84: LED55.anode, R67.Pin_0
  N85: LED56.anode, R66.Pin_0
  N86: LED57.anode, R68.Pin_0
  N87: LED58.anode, R69.Pin_0
  N88: R71.Pin_0, LED64.anode
  N89: R72.Pin_0, LED60.anode
  N90: R73.Pin_0, LED63.anode
  N91: R74.Pin_0, LED59.anode
  N92: R75.Pin_0, LED62.anode
  N93: R76.Pin_0, LED65.anode
  N94: R77.Pin_0, LED66.anode
  N95: R78.Pin_0, LED61.anode
  N96: LED59.cathode, LED60.cathode, LED61.cathode, LED62.cathode, LED63.cathode, LED64.cathode, LED65.cathode, LED66.cathode
  N97: R79.Pin_1, Q10.B
  N98: R80.Pin_1, Q9.B

notes:
  Porque Potenciometros?
  Os Potenciomentros é uma segunda proposta substituindo os botões que selecionam a intencidade da luz e o tempo.
  LCD
  Usado um LCD Comum
  Não temos ainda um LCD i2C
  que ajudaria a sobrar mais pinos.
  19V
  2A
  Tendo dois pwm a mais, podemos usa-los para controlarmos 4 barramentos de leds de forma independetes, ou seja dois em cima dois em baixo, porém somente temos 2 PWM livres devido o uso do LCD.
